# Fritzing sketch beatdetector (saved by Fritzing 0.4.3b)
breadboards: 1

parts:
  Arduino1 = Arduino
  LED1 = Red LED - 5mm
  330 = 330 Ω Resistor [package=THT]
  330_2 = 330 Ω Resistor [package=THT]
  Listen_Switch = Pushbutton [package="[THT]"]
  LED2 = green LED - 5mm
  Beat_Switch = Pushbutton [package="[THT]"]
  10k = 10k Ω Resistor [package=THT]
  10k_2 = 10k Ω Resistor [package=THT]

nets:
  N1: Arduino1.GND, 330.Pin_1, 330_2.Pin_1, 10k.Pin_1, 10k_2.Pin_1
  N2: Arduino1.D5, Listen_Switch.Pin_3, Listen_Switch.Pin_4, 10k.Pin_0
  N3: Arduino1.D4, LED2.anode
  N4: Arduino1.D3, LED1.anode
  N5: Arduino1.D2, Beat_Switch.Pin_3, Beat_Switch.Pin_4, 10k_2.Pin_0
  N6: Arduino1.+5V, Listen_Switch.Pin_1, Listen_Switch.Pin_2, Beat_Switch.Pin_1, Beat_Switch.Pin_2
  N7: LED1.cathode, 330_2.Pin_0
  N8: 330.Pin_0, LED2.cathode
